// Logisim project CPU Design.circ as structural Verilog: 2 circuits, main circuit main
module main (
);

  Multiplexer multiplexer_1 ();  // open: in0, in1, out, sel, en
endmodule

module ALU (
  input  [2:0] OP,
  input  [7:0] A,
  input  [7:0] B,
  input  Carry,
  output [7:0] Result,
  output Z,
  output N,
  output C,
  output V
);

  wire [7:0] adder_1_out, and_1_out, not_1_out, or_1_out, shifter_1_out, shifter_2_out, subtractor_1_out,
       xor_1_out;

  Adder adder_1 (.a(A), .b(B), .out(adder_1_out), .cin(Carry), .cout(C));
  Subtractor subtractor_1 (.a(A), .b(B), .out(subtractor_1_out), .bin(Carry), .bout(C));
  assign and_1_out = A & B;  // AND_Gate and_1, 8 bits wide
  assign or_1_out = A | B;  // OR_Gate or_1, 8 bits wide
  assign xor_1_out = A ^ B;  // XOR_Gate xor_1, 8 bits wide
  assign not_1_out = ~A;  // NOT_Gate not_1, 8 bits wide
  Shifter shifter_1 (.in(A), .out(shifter_1_out));  // open: dist
  Shifter #(.shift("lr")) shifter_2 (.in(A), .out(shifter_2_out));  // open: dist
  // Probe on C
  Multiplexer #(.select(3), .width(8), .enable("false")) multiplexer_1 (
    .in0(adder_1_out), .in1(subtractor_1_out), .in2(and_1_out), .in3(or_1_out), .in4(xor_1_out),
    .in5(not_1_out), .in6(shifter_1_out), .in7(shifter_2_out), .out({N, Result[6:0]}), .sel(OP));
  nor nor_1 (Z, Result[0], Result[1], Result[2], Result[3], Result[4], Result[5], Result[6], N);

  assign Result[7] = N;
endmodule
